# Fritzing sketch spicerack (saved by Fritzing 0.9.3b)
breadboards: 3

parts:
  BeagleBone1 = BeagleBone Black
  Part1 = EasyDriver_v44
  M1 = Stepper Motor - Bipolar
  R1 = Resistor [tolerance=±5% resistance=220 package="2512 [SMD]"]
  R2 = Resistor [tolerance=±5% resistance=220 package="2010 [SMD]"]
  LED1 = smd LED [color="Red (633nm)" package="1206 [SMD]"]
  LED2 = smd LED [color="Green (555nm)" package="1206 [SMD]"]
  Launchpad2 = LaunchPad EK-TM4C123GXL
  TFT1 = 1.8" TFT Display with uSD
  R3 = Resistor [tolerance=±5% resistance=220 package="1206 [SMD]"]
  R4 = Resistor [tolerance=±5% resistance=220 package="2512 [SMD]"]
  R5 = Resistor [tolerance=±5% resistance=220 package="2512 [SMD]"]
  R6 = Resistor [tolerance=±5% resistance=220 package="2512 [SMD]"]

nets:
  N1: BeagleBone1.no_name_yet#6, Part1.V+
  N2: BeagleBone1.no_name_yet#101, BeagleBone1.no_name_yet#102, Part1.GND, LED1.cathode, LED2.cathode
  N3: BeagleBone1.no_name_yet#107, R5.Pin_1
  N4: BeagleBone1.no_name_yet#108, R6.Pin_1
  N5: BeagleBone1.no_name_yet#109, R3.Pin_0
  N6: BeagleBone1.no_name_yet#110, R4.Pin_0
  N7: BeagleBone1.no_name_yet#111, Part1.ENABLE
  N8: BeagleBone1.no_name_yet#112, Part1.MS1
  N9: BeagleBone1.no_name_yet#113, Part1.MS2
  N10: BeagleBone1.no_name_yet#114, Part1.STEP
  N11: BeagleBone1.no_name_yet#116, Part1.DIR
  N12: BeagleBone1.no_name_yet#125, R1.Pin_1
  N13: BeagleBone1.no_name_yet#128, R2.Pin_1
  N14: Part1.OUT2A, M1.A
  N15: Part1.OUT2B, M1.C
  N16: Part1.OUT1A, M1.B
  N17: Part1.OUT1B, M1.D
  N18: R1.Pin_0, LED2.anode
  N19: R2.Pin_0, LED1.anode
  N20: Launchpad2.pin_1, TFT1.MISO, TFT1.GND
  N21: Launchpad2.pin_8, TFT1.D/C
  N22: Launchpad2.pin_9, TFT1.MOSI
  N23: Launchpad2.pin_10, TFT1.SCK
  N24: Launchpad2.pin_11, TFT1.RST
  N25: Launchpad2.pin_12, TFT1.SDCS
  N26: Launchpad2.pin_22, TFT1.BL
  N27: Launchpad2.pin_23, R5.Pin_0
  N28: Launchpad2.pin_24, R6.Pin_0
  N29: Launchpad2.pin_25, R3.Pin_1
  N30: Launchpad2.pin_26, R4.Pin_1

custom parts:
  BeagleBone Black: BeagleBone Black rev. A5B
  1.8" TFT Display with uSD: 1.8" TFT Display with SPI control and MicroSD card
